# Fritzing sketch SparkFun_MotionControlledWearableLEDDanceHarnessCircuitComplete_Fritzing_Back_View (saved by Fritzing 0.9.3b)
breadboards: 1

parts:
  RGB_Strip_LED1 = RGB Strip LED
  RGB_Strip_LED2 = RGB Strip LED
  RGB_Strip_LED3 = RGB Strip LED
  RGB_Strip_LED4 = RGB Strip LED
  RGB_Strip_LED5 = RGB Strip LED
  RGB_Strip_LED6 = RGB Strip LED
  RGB_Strip_LED7 = RGB Strip LED
  RGB_Strip_LED8 = RGB Strip LED
  RGB_Strip_LED9 = RGB Strip LED
  RGB_Strip_LED10 = RGB Strip LED
  Part4 = Arduino Pro Mini v13
  VCC2 = Battery block 9V
  JACK1 = 2.1mm DC Barrel Jack
  Part6 = Triple Axis Accelerometer Breakout - ADXL335
  Q5 = MOSFET-NCHANNEL [package=to220v]
  J1 = Power Plug
  R4 = Resistor [package="2512 [SMD]"]

nets:
  N1: RGB_Strip_LED1.Common_Connect#4, RGB_Strip_LED6.Common_Connect#4, Part4.RAW, JACK1.center
  N2: RGB_Strip_LED1.Blue_Connect#5, RGB_Strip_LED1.Red_Connect#6, RGB_Strip_LED6.Blue_Connect#5, RGB_Strip_LED6.Red_Connect#6, Q5.D
  N3: RGB_Strip_LED1.Green_Connect#7, RGB_Strip_LED6.Green_Connect#7
  N4: RGB_Strip_LED2.Common_Connect#4, RGB_Strip_LED4.Common_Connect#4
  N5: RGB_Strip_LED2.Blue_Connect#5, RGB_Strip_LED4.Green_Connect#7
  N6: RGB_Strip_LED2.Red_Connect#6, RGB_Strip_LED4.Red_Connect#6
  N7: RGB_Strip_LED2.Green_Connect#7, RGB_Strip_LED4.Blue_Connect#5
  N8: RGB_Strip_LED3.Common_Connect#4, RGB_Strip_LED5.Common_Connect#4
  N9: RGB_Strip_LED3.Blue_Connect#5, RGB_Strip_LED5.Green_Connect#7
  N10: RGB_Strip_LED3.Red_Connect#6, RGB_Strip_LED5.Red_Connect#6
  N11: RGB_Strip_LED3.Green_Connect#7, RGB_Strip_LED5.Blue_Connect#5
  N12: RGB_Strip_LED7.Common_Connect#4, RGB_Strip_LED10.Common_Connect#4
  N13: RGB_Strip_LED7.Blue_Connect#5, RGB_Strip_LED10.Green_Connect#7
  N14: RGB_Strip_LED7.Red_Connect#6, RGB_Strip_LED10.Red_Connect#6
  N15: RGB_Strip_LED7.Green_Connect#7, RGB_Strip_LED10.Blue_Connect#5
  N16: RGB_Strip_LED8.Common_Connect#4, RGB_Strip_LED9.Common_Connect#4
  N17: RGB_Strip_LED8.Blue_Connect#5, RGB_Strip_LED9.Green_Connect#7
  N18: RGB_Strip_LED8.Red_Connect#6, RGB_Strip_LED9.Red_Connect#6
  N19: RGB_Strip_LED8.Green_Connect#7, RGB_Strip_LED9.Blue_Connect#5
  GND: Part4.GND, JACK1.switch, Part6.GND, Q5.S, R4.Pin_0
  VCC: Part4.VCC, Part6.VCC
  N20: Part4.A2, Part6.XOUT
  N21: Part4.A1, Part6.YOUT
  N22: Part4.A0, Part6.ZOUT
  N23: Part4.D11_PWM/MOSI, Q5.G, R4.Pin_1
  N24: VCC2.-, J1.GND, J1.tip_GND
  N25: VCC2.+, J1.PWR, J1.tip_PWR

notes:
  Right - LED Segment A
  Right - LED Segment B
  Right - LED Segment C
  Left - LED Segment A
  Left - LED Segment B
  Left - LED Segment C
  Use Male Barrel Jack Adapter Cable Here
  Back View - The transparent components are mirrored image of the accelerometer, resistor, and N Channel MOSFET soldered on the back of the solderable breadboard. When flipping the board to view the back, the connections between each node will be the same. Wires should be sandwiched between the boards.
  Make sure to check your connections before powering up!

custom parts:
  RGB Strip LED: A tri-color Strip LED with red, green and blue. Pin order: red - common cathode - blue - green
  RGB Strip LED: A tri-color Strip LED with red, green and blue. Pin order: red - common cathode - blue - green
  RGB Strip LED: A tri-color Strip LED with red, green and blue. Pin order: red - common cathode - blue - green
  2.1mm DC Barrel Jack: 2.1mm DC Barrel Jack with Thru-Hole Connectors (breadboardable)
  Triple Axis Accelerometer Breakout - ADXL335: Accelerometer for sensing three-dimensional orientation/acceleration on a breakout board. Compatible to the ADXL3xx series of sensor chips.
  MOSFET-NCHANNEL: Generic NMOS footprint
  Power Plug: Power Jack This is the standard 5.5mm barrel plug for power. This part has bendable leads (i.e. wires in the real world) to connect to wall warts or the breadboard in the standard wire end, and hidden connectors on the tip end that will connect when "plugged in" (overlapped with the jack so it appears "plugged in" in breadboard) to the modified coax jack part. Internal busses connect the two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
  Resistor: Resistor Basic schematic elements and footprints for 0603, 1206, and PTH resistors.
