# Fritzing sketch SparkFun_MotionControlledWearableLEDDanceHarnessCircuitComplete_Fritzing_Front_View (saved by Fritzing 0.9.3b)
breadboards: 1

parts:
  RGB_Strip_LED1 = RGB Strip LED
  RGB_Strip_LED2 = RGB Strip LED
  RGB_Strip_LED3 = RGB Strip LED  # not connected
  RGB_Strip_LED4 = RGB Strip LED
  RGB_Strip_LED5 = RGB Strip LED
  RGB_Strip_LED6 = RGB Strip LED
  RGB_Strip_LED7 = RGB Strip LED
  RGB_Strip_LED8 = RGB Strip LED
  RGB_Strip_LED9 = RGB Strip LED
  RGB_Strip_LED10 = RGB Strip LED  # not connected
  VCC2 = Battery block 9V
  J2 = Power Plug
  Q8 = MOSFET-NCHANNEL [package=to220v]
  R5 = Resistor [tolerance=±5% resistance=10k package="2512 [SMD]"]
  Part9 = Triple Axis Accelerometer Breakout - ADXL335
  JACK4 = 2.1mm DC Barrel Jack
  Part10 = Arduino Pro Mini v13
  RGB_Strip_LED11 = RGB Strip LED
  RGB_Strip_LED12 = RGB Strip LED

nets:
  N1: RGB_Strip_LED1.Common_Connect#4, RGB_Strip_LED5.Common_Connect#4
  N2: RGB_Strip_LED1.Blue_Connect#5, RGB_Strip_LED5.Green_Connect#7
  N3: RGB_Strip_LED1.Red_Connect#6, RGB_Strip_LED5.Red_Connect#6
  N4: RGB_Strip_LED1.Green_Connect#7, RGB_Strip_LED5.Blue_Connect#5
  N5: RGB_Strip_LED2.Common_Connect#4, RGB_Strip_LED12.Common_Connect#4
  N6: RGB_Strip_LED2.Blue_Connect#5, RGB_Strip_LED12.Green_Connect#7
  N7: RGB_Strip_LED2.Red_Connect#6, RGB_Strip_LED12.Red_Connect#6
  N8: RGB_Strip_LED2.Green_Connect#7, RGB_Strip_LED12.Blue_Connect#5
  N9: RGB_Strip_LED4.Common_Connect#4, RGB_Strip_LED8.Common_Connect#4, JACK4.center, Part10.RAW
  N10: RGB_Strip_LED4.Blue_Connect#5, RGB_Strip_LED8.Blue_Connect#5
  GND: RGB_Strip_LED4.Red_Connect#6, RGB_Strip_LED4.Green_Connect#7, RGB_Strip_LED8.Red_Connect#6, RGB_Strip_LED8.Green_Connect#7, Q8.G, Q8.D, Q8.S, R5.Pin_0, R5.Pin_1, Part9.GND, JACK4.switch, Part10.GND, Part10.D11_PWM/MOSI
  N11: RGB_Strip_LED6.Common_Connect#4, RGB_Strip_LED7.Common_Connect#4
  N12: RGB_Strip_LED6.Blue_Connect#5, RGB_Strip_LED7.Green_Connect#7
  N13: RGB_Strip_LED6.Red_Connect#6, RGB_Strip_LED7.Red_Connect#6
  N14: RGB_Strip_LED6.Green_Connect#7, RGB_Strip_LED7.Blue_Connect#5
  N15: RGB_Strip_LED9.Common_Connect#4, RGB_Strip_LED11.Common_Connect#4
  N16: RGB_Strip_LED9.Blue_Connect#5, RGB_Strip_LED11.Green_Connect#7
  N17: RGB_Strip_LED9.Red_Connect#6, RGB_Strip_LED11.Red_Connect#6
  N18: RGB_Strip_LED9.Green_Connect#7, RGB_Strip_LED11.Blue_Connect#5
  N19: VCC2.-, J2.GND, J2.tip_GND
  N20: VCC2.+, J2.PWR, J2.tip_PWR
  N21: Part9.ZOUT, Part10.A0
  N22: Part9.YOUT, Part10.A1
  N23: Part9.XOUT, Part10.A2
  VCC: Part9.VCC, Part10.VCC

notes:
  Left - LED Segment A
  Left - LED Segment B
  Left - LED Segment C
  Right - LED Segment A
  Right - LED Segment B
  Right - LED Segment C
  Use Male Barrel Jack Adapter Cable Here
  Front View - The transparent components are mirrored image of the Arduino Pro Mini and barrel jack soldered on the front of the solderable breadboard. When flipping the board to view the front, the connections between each node will be the same. Wires should be sandwiched between the boards.
  Make sure to check your connections before powering up!

custom parts:
  RGB Strip LED: A tri-color Strip LED with red, green and blue. Pin order: red - common cathode - blue - green
  RGB Strip LED: A tri-color Strip LED with red, green and blue. Pin order: red - common cathode - blue - green
  RGB Strip LED: A tri-color Strip LED with red, green and blue. Pin order: red - common cathode - blue - green
  Power Plug: Power Jack This is the standard 5.5mm barrel plug for power. This part has bendable leads (i.e. wires in the real world) to connect to wall warts or the breadboard in the standard wire end, and hidden connectors on the tip end that will connect when "plugged in" (overlapped with the jack so it appears "plugged in" in breadboard) to the modified coax jack part. Internal busses connect the two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
  2.1mm DC Barrel Jack: 2.1mm DC Barrel Jack with Thru-Hole Connectors (breadboardable)
  Arduino Pro Mini v13: It's blue! It's thin! It's the Arduino Pro Mini! SparkFun's minimal design approach to Arduino. This is a 5V Arduino running the 16MHz bootloader. Arduino Pro Mini does not come with connectors populated so that you can solder in any connector or wire with any orientation you need. We recommend first time Arduino users start with the Uno R3. It's a great board that will get you up and running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
