# Fritzing sketch SparkFun_MotionControlledWearableLEDDanceHarnessCircuit_Fritzing (saved by Fritzing 0.9.3b)
breadboards: 2

parts:
  RGB_Strip_LED1 = RGB Strip LED
  Q3 = Basic FET N-Channel [package="D2Pak [SMD]"]
  Part2 = Triple Axis Accelerometer Breakout - ADXL335
  Part3 = Arduino Pro Mini v13
  R1 = Resistor [tolerance=±5% resistance=10k package="0805 [SMD]"]
  VCC1 = Battery block 9V
  RGB_Strip_LED2 = RGB Strip LED  # not connected
  JACK1 = 2.1mm DC Barrel Jack
  J1 = Power Plug

nets:
  N1: RGB_Strip_LED1.Common_Connect#4, Part3.RAW, JACK1.center
  N2: RGB_Strip_LED1.Blue_Connect#5, RGB_Strip_LED1.Red_Connect#6, Q3.drain
  N3: Q3.Gate, Part3.D11_PWM/MOSI, R1.Pin_0
  GND: Q3.source, Part2.GND, Part3.GND, R1.Pin_1, JACK1.sleeve
  N4: Part2.ZOUT, Part3.A0
  N5: Part2.YOUT, Part3.A1
  N6: Part2.XOUT, Part3.A2
  VCC: Part2.VCC, Part3.VCC
  N7: VCC1.-, J1.GND, J1.tip_GND
  N8: VCC1.+, J1.PWR, J1.tip_PWR

notes:
  Use Male Barrel Jack Adapter Cable Here

custom parts:
  RGB Strip LED: A tri-color Strip LED with red, green and blue. Pin order: red - common cathode - blue - green
  2.1mm DC Barrel Jack: 2.1mm DC Barrel Jack with Thru-Hole Connectors (breadboardable)
  Power Plug: Power Jack This is the standard 5.5mm barrel plug for power. This part has bendable leads (i.e. wires in the real world) to connect to wall warts or the breadboard in the standard wire end, and hidden connectors on the tip end that will connect when "plugged in" (overlapped with the jack so it appears "plugged in" in breadboard) to the modified coax jack part. Internal busses connect the two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
